// Logisim project somadorUso.circ as structural Verilog: 2 circuits, main circuit somador4bits
module somador4bits (
  input  a3,
  input  a2,
  input  a1,
  input  a0,
  input  b3,
  input  b2,
  input  b1,
  input  b0,
  input  C0,
  output out_10,
  output out_11,
  output out_12,
  output out_13,
  output out_14
);
endmodule

module somador8bits (
  input  oprtn,
  output ovflw,
  output [7:0] res
);

  wire xor_1_out, xor_2_out, xor_3_out, xor_4_out, xor_5_out, xor_6_out, xor_7_out, xor_8_out;
  wire [7:0] a_out, b_out;

  Slider a (.out(a_out));
  Slider b (.out(b_out));
  xor xor_1 (xor_1_out, b_out[0], oprtn);
  xor xor_2 (xor_2_out, b_out[1], oprtn);
  xor xor_3 (xor_3_out, b_out[2], oprtn);
  xor xor_4 (xor_4_out, b_out[3], oprtn);
  xor xor_5 (xor_5_out, b_out[4], oprtn);
  xor xor_6 (xor_6_out, b_out[5], oprtn);
  xor xor_7 (xor_7_out, b_out[6], oprtn);
  xor xor_8 (xor_8_out, b_out[7], oprtn);
endmodule
